// Logisim project p4.circ as structural Verilog: 34 circuits, main circuit main
module main (
  input  [2:0] PROGRAM_SELECT,
  input  RESET
);

  wire ALUSrc, answer_1_power_out, CLOCK, DONE, IsADD, IsB, IsBLink, IsBXLR, IsCMP, IsLDR, IsMov, IsSTR,
       IsSUB, MemtoReg, MemWrite, PCSrc, RegWrite;
  wire [1:0] ALUControl, controller_1_regsrc, ImmSrc, n27_26_1__27_26;
  wire [3:0] A1, A2, A3, n15_12_1__15_12, n31_28_1__31_28, NZCV;
  wire [5:0] n25_20_1__25_20;
  wire [9:0] visualizer_1_out_14, visualizer_1_out_14_2, visualizer_1_out_17, visualizer_1_out_17_2,
       visualizer_1_out_18, visualizer_1_out_18_2;
  wire [19:0] visualizer_1_out_10, visualizer_1_out_11, visualizer_1_out_12, visualizer_1_out_13,
       visualizer_1_out_15, visualizer_1_out_16;
  wire [23:0] n23_0_1_out_2, n23_0_2_out_2;
  wire [31:0] _32_1, _32_2, alu_condition_flags_1__32_out, answer_1_answer, datamemory_1_read_data,
       extender_1__32_out, IW, multiplexer_1_out, multiplexer_2_out, PC, PC_4, PC_8, r0, r1, r2, r3, r4, r5,
       r6, r7, r8, r9, r10, r11, r12, r13, r14, r15, register_file_1_r1_2, register_file_1_r2_2,
       registerlogic_1_r15, registerlogic_1_wd3;

  // Probe on r0
  // Probe on r1
  // Probe on r2
  // Probe on r3
  // Probe on r4
  // Probe on r5
  // Probe on r6
  // Probe on r7
  // Probe on PC
  // Probe on PC_4
  // Probe on PC_8
  Multiplexer #(.width(32), .disabled(0), .enable("false")) multiplexer_1 (
    .in0(PC_4), .in1(multiplexer_2_out), .out(multiplexer_1_out), .sel(PCSrc));
  PC_Gate pc_gate_1 (.PC(multiplexer_1_out), .CLock(CLOCK), .Reset(RESET), .PC_OUT(PC));
  Is_Done is_done_1 (.PCSrc(PCSrc), .OLD_PC(PC), .NEW_PC(multiplexer_2_out), .DONE(DONE));
  // Probe on r8
  // Probe on r9
  // Probe on r10
  // Probe on r11
  // Probe on r12
  // Probe on r13
  // Probe on r14
  // Probe on r15
  // Probe on IW
  // Probe on _32_1
  CheckADDSUB checkaddsub_1 (.IW(IW), .IsAdd(IsADD), .IsSub(IsSUB));
  PC_Adder pc_adder_1 (.PC(PC), .PC_8(PC_8), .PC_4(PC_4));
  // Probe on A1
  // Probe on A2
  // Probe on A3
  // Probe on _32_2
  Instruction_Memory instruction_memory_1 (.Address_PC(PC), ._32_OUT(IW), .PROGRAM(PROGRAM_SELECT));
  // Probe on PCSrc
  // Probe on MemtoReg
  // Probe on MemWrite
  // Probe on ALUSrc
  // Probe on ImmSrc
  // Probe on RegWrite
  // Probe on IsMov
  // Probe on ALUControl
  _31_28 u_31_28_1 (.IW(IW), ._31_28(n31_28_1__31_28));
  _27_26 u_27_26_1 (.IW(IW), ._27_26(n27_26_1__27_26));
  _25_20 u_25_20_1 (.IW(IW), ._25_20(n25_20_1__25_20));
  _15_12 u_15_12_1 (.IW(IW), ._15_12(n15_12_1__15_12));
  _23_0 u_23_0_1 (.IW(IW), .out_2(n23_0_1_out_2));
  // Probe on IsBLink
  // Probe on IsCMP
  // Probe on IsBXLR
  // Probe on DONE
  // Probe on IsSTR
  // Probe on IsLDR
  // Probe on IsB
  // Probe on IsSUB
  // Probe on IsADD
  Controller controller_1 (
    .RD(n15_12_1__15_12), .OP(n27_26_1__27_26), .Funct(n25_20_1__25_20), .MemtoReg(MemtoReg),
    .ALUSrc(ALUSrc), .ImmSrc(ImmSrc), .ALUControl(ALUControl), .Cond(n31_28_1__31_28), .CLOCK(CLOCK),
    .ALUFlags(NZCV), .RegSrc(controller_1_regsrc), .PCSrc(PCSrc), .RegWrite(RegWrite), .MemWrite(MemWrite),
    .imm24(n23_0_1_out_2), .IsMov(IsMov), .IsBLink(IsBLink), .IsCMP(IsCMP), .IsBXLR(IsBXLR), .IW(IW),
    .IsLDR(IsLDR), .IsSTR(IsSTR), .IsB(IsB));
  RegisterLogic registerlogic_1 (
    .IW(IW), .A1(A1), .A2(A2), ._0Bit(controller_1_regsrc[0]), ._1Bit(controller_1_regsrc[1]), .A3(A3),
    .WD3(registerlogic_1_wd3), .OUTPUT(multiplexer_2_out), .IsBLink(IsBLink), .PC_4(PC_4), .IsBXLR(IsBXLR),
    .r14(r14), .PC_8(PC_8), .r15(registerlogic_1_r15));
  Clock u_CLOCK (.out(CLOCK));
  // Probe on NZCV
  Register_File register_file_1 (
    .WD3(registerlogic_1_wd3), .WE(RegWrite), .R15(registerlogic_1_r15), .A1(A1), .A2(A2), .CLOCK(CLOCK),
    .RESET(RESET), .A3(A3), .R1_2(register_file_1_r1_2), .R2_2(register_file_1_r2_2), .r14(r14), .r15_2(r15),
    .r13(r13), .r12(r12), .r11(r11), .r10(r10), .r9(r9), .r8(r8), .r7(r7), .r6(r6), .r5(r5), .r4(r4),
    .r3(r3), .r2(r2), .r1(r1), .r0(r0));
  // Probe on multiplexer_2_out
  _23_0 u_23_0_2 (.IW(IW), .out_2(n23_0_2_out_2));
  DotMatrix #(.matrixcols(6), .matrixrows(10)) dotmatrix_1 (
    .col0(visualizer_1_out_10[19:10]), .col1(visualizer_1_out_10[9:0]), .col2(visualizer_1_out_11[19:10]),
    .col3(visualizer_1_out_11[9:0]), .col4(visualizer_1_out_12[19:10]), .col5(visualizer_1_out_12[9:0]));
  Visualizer visualizer_1 (
    .Is_LDR(IsSTR), .Is_STR(IsLDR), .Is_ADD(IsADD), .Is_SUB(IsSUB), .Is_Mov(IsMov), .Is_B(IsB),
    .Is_BL(IsBLink), .Is_BX(IsBXLR), .out_10(visualizer_1_out_10), .out_11(visualizer_1_out_11),
    .out_12(visualizer_1_out_12), .out_13(visualizer_1_out_13),
    .out_14({visualizer_1_out_14_2, visualizer_1_out_14}), .out_15(visualizer_1_out_15),
    .out_16(visualizer_1_out_16), .out_17({visualizer_1_out_17_2, visualizer_1_out_17}),
    .out_18({visualizer_1_out_18_2, visualizer_1_out_18}), .Is_CMP(IsCMP));
  DotMatrix #(.matrixcols(6), .matrixrows(10)) dotmatrix_2 (
    .col0(visualizer_1_out_13[19:10]), .col1(visualizer_1_out_13[9:0]), .col2(visualizer_1_out_14_2),
    .col3(visualizer_1_out_14), .col4(visualizer_1_out_15[19:10]), .col5(visualizer_1_out_15[9:0]));
  // Probe on extender_1__32_out
  Extender extender_1 (._24_IN(n23_0_2_out_2), .ImmSrc(ImmSrc), ._32_OUT(extender_1__32_out));
  DotMatrix #(.matrixcols(6), .matrixrows(10)) dotmatrix_3 (
    .col0(visualizer_1_out_16[19:10]), .col1(visualizer_1_out_16[9:0]), .col2(visualizer_1_out_17_2),
    .col3(visualizer_1_out_17), .col4(visualizer_1_out_18_2), .col5(visualizer_1_out_18));
  ALU_PreLogic alu_prelogic_1 (
    .IsMov(IsMov), .R1(register_file_1_r1_2), .R2(register_file_1_r2_2), .IsBXLR(IsBXLR), ._32_1(_32_1),
    ._32_2(_32_2), .ALUSrc(ALUSrc), .EXTEND(extender_1__32_out));
  // Probe on multiplexer_2_out
  ALU_Condition_Flags alu_condition_flags_1 (
    ._32_A(_32_1), ._32_B(_32_2), ._32_OUT(alu_condition_flags_1__32_out), .ZERO___Z(NZCV[2]),
    .CARRY___C(NZCV[1]), .NEGATIVE___N(NZCV[3]), .OVERFLOW___V(NZCV[0]), .ALU_Coltrol(ALUControl));
  DataMemory datamemory_1 (
    .clk(CLOCK), .WE(MemWrite), .RESET(RESET), .Address(alu_condition_flags_1__32_out),
    .WORD(register_file_1_r2_2), .Read_Data(datamemory_1_read_data));
  // Probe on datamemory_1_read_data
  // Probe on alu_condition_flags_1__32_out
  LED led_1 (.in(answer_1_power_out));
  LED led_2 (.in(answer_1_power_out));
  LED led_3 (.in(answer_1_power_out));
  LED led_4 (.in(answer_1_power_out));
  LED led_5 (.in(answer_1_power_out));
  LED led_6 (.in(answer_1_power_out));
  LED led_7 (.in(answer_1_power_out));
  LED led_8 (.in(answer_1_power_out));
  LED led_9 (.in(answer_1_power_out));
  LED led_10 (.in(answer_1_power_out));
  LED led_11 (.in(answer_1_power_out));
  LED led_12 (.in(answer_1_power_out));
  Multiplexer #(.width(32), .disabled(0), .enable("false")) multiplexer_2 (
    .in0(alu_condition_flags_1__32_out), .in1(datamemory_1_read_data), .out(multiplexer_2_out), .sel(MemtoReg));
  LED led_13 (.in(answer_1_power_out));
  LED led_14 (.in(answer_1_power_out));
  LED led_15 (.in(answer_1_power_out));
  LED led_16 (.in(answer_1_power_out));
  LED led_17 (.in(answer_1_power_out));
  LED led_18 (.in(answer_1_power_out));
  LED led_19 (.in(answer_1_power_out));
  ANSWER answer_1 (.r0(r0), .ANSWER(answer_1_answer), .POWER_OUT(answer_1_power_out), ._2_In({CLOCK, DONE}));
  // Probe on answer_1_answer
  LED led_20 (.in(answer_1_power_out));
  LED led_21 (.in(answer_1_power_out));
  LED led_22 (.in(answer_1_power_out));
  LED led_23 (.in(answer_1_power_out));
  LED led_24 (.in(answer_1_power_out));
  LED led_25 (.in(answer_1_power_out));
  LED led_26 (.in(answer_1_power_out));
endmodule

module ALU (
  input  [1:0] ALU_Coltrol,
  input  [31:0] _32_A,
  input  [31:0] _32_B,
  output [31:0] _32_OUT
);

  wire [31:0] adder_1_out, and_1_out, or_1_out, subtractor_1_out;

  // Probe on _32_A
  // Probe on _32_B
  Adder #(.width(32)) adder_1 (.a(_32_A), .b(_32_B), .out(adder_1_out));  // open: cin, cout
  Subtractor #(.width(32)) subtractor_1 (.a(_32_A), .b(_32_B), .out(subtractor_1_out));  // open: bin, bout
  assign and_1_out = _32_A & _32_B;  // AND_Gate and_1, 32 bits wide
  assign or_1_out = _32_A | _32_B;  // OR_Gate or_1, 32 bits wide
  Multiplexer #(.select(2), .width(32)) multiplexer_1 (
    .in0(adder_1_out), .in1(subtractor_1_out), .in2(and_1_out), .in3(or_1_out), .out(_32_OUT),
    .sel(ALU_Coltrol));  // open: en
  // Probe on _32_OUT
endmodule

module Instruction_Memory (
  input  [2:0] PROGRAM,
  input  [31:0] Address_PC,
  output [31:0] _32_OUT
);

  wire [31:0] rom_1_data, rom_2_data, rom_3_data, rom_4_data, rom_5_data, rom_6_data, rom_7_data, rom_8_data;

  // Probe on Address_PC
  ROM #(.dataWidth(32)) rom_1 (.addr(Address_PC[9:2]), .data(rom_1_data), .sel(1'b1));
  ROM #(.dataWidth(32)) rom_2 (.addr(Address_PC[9:2]), .data(rom_2_data), .sel(1'b1));
  ROM #(.dataWidth(32)) rom_3 (.addr(Address_PC[9:2]), .data(rom_3_data), .sel(1'b1));
  ROM #(.dataWidth(32)) rom_4 (.addr(Address_PC[9:2]), .data(rom_4_data), .sel(1'b1));
  ROM #(.dataWidth(32)) rom_5 (.addr(Address_PC[9:2]), .data(rom_5_data), .sel(1'b1));
  ROM #(.dataWidth(32)) rom_6 (.addr(Address_PC[9:2]), .data(rom_6_data), .sel(1'b1));
  ROM #(.dataWidth(32)) rom_7 (.addr(Address_PC[9:2]), .data(rom_7_data), .sel(1'b1));
  ROM #(.dataWidth(32)) rom_8 (.addr(Address_PC[9:2]), .data(rom_8_data), .sel(1'b1));
  Multiplexer #(.select(3), .width(32), .disabled(0), .enable("false")) multiplexer_1 (
    .in0(rom_1_data), .in1(rom_2_data), .in2(rom_3_data), .in3(rom_4_data), .in4(rom_5_data),
    .in5(rom_6_data), .in6(rom_7_data), .in7(rom_8_data), .out(_32_OUT), .sel(PROGRAM));

  // Other names for the same wires on the sheet: PC[7:0] = Address_PC[9:2]

  // Notes on the sheet:
  //   SumArray (1,2,3,4,5)
  //   SumArray(6, 7, 8, 910)
  //   FibIter (15)
  //   FibIter (25)
  //   FibRec (5)
  //   FibRec (7)
  //   FibRec(15)
  //   TESTER SET
  //   contents of rom_1 (hex, n*v repeats v):
  //   e3a0d080 e08dd00d e08dd00d e24dd004 e3a00001 e58d0000 e24dd004 e3a00002 e58d0000 e24dd004 e3a00003
  //   e58d0000 e24dd004 e3a00004 e58d0000 e24dd004 e3a00005 e58d0000 e1a0000d e3a01005 eb000000 eafffffe
  //   e3a02000 e1a03000 e3a04000 e1520001 aa000004 e5935000 e0844005 e2822001 e2833004 eafffff8 e1a00004
  //   e12fff1e
  //   contents of rom_2 (hex, n*v repeats v):
  //   e3a0d080 e08dd00d e08dd00d e24dd004 e3a00006 e58d0000 e24dd004 e3a00007 e58d0000 e24dd004 e3a00008
  //   e58d0000 e24dd004 e3a00009 e58d0000 e24dd004 e3a0000a e58d0000 e1a0000d e3a01005 eb000000 eafffffe
  //   e3a02000 e1a03000 e3a04000 e1520001 aa000004 e5935000 e0844005 e2822001 e2833004 eafffff8 e1a00004
  //   e12fff1e
  //   contents of rom_3 (hex, n*v repeats v):
  //   e3a0000f eb000000 eafffffe e3a01000 e3a02001 e3a03000 e3500000 3a03000 a00000c e3500001 3a03001
  //   a000009 e3a04002 e1a05000 eaffffff e1540005 ca000004 e0813002 e1a01002 e1a02003 e2844001 eafffff8
  //   e1a00003 e12fff1e
  //   contents of rom_4 (hex, n*v repeats v):
  //   e3a00019 eb000000 eafffffe e3a01000 e3a02001 e3a03000 e3500000 3a03000 a00000c e3500001 3a03001
  //   a000009 e3a04002 e1a05000 eaffffff e1540005 ca000004 e0813002 e1a01002 e1a02003 e2844001 eafffff8
  //   e1a00003 e12fff1e
  //   contents of rom_5 (hex, n*v repeats v):
  //   e3a00005 e3a0d080 e08dd00d e08dd00d eb000000 eafffffe e24dd004 e58d4000 e24dd004 e58d5000 e24dd004
  //   e58de000 e3500001 ca000000 ea000007 e1a04000 e2400001 ebfffff3 e1a05000 e1a00004 e2400002 ebffffef
  //   e0850000 e59de000 e28dd004 e59d5000 e28dd004 e59d4000 e28dd004 e12fff1e
  //   contents of rom_6 (hex, n*v repeats v):
  //   e3a00007 e3a0d080 e08dd00d e08dd00d eb000000 eafffffe e24dd004 e58d4000 e24dd004 e58d5000 e24dd004
  //   e58de000 e3500001 ca000000 ea000007 e1a04000 e2400001 ebfffff3 e1a05000 e1a00004 e2400002 ebffffef
  //   e0850000 e59de000 e28dd004 e59d5000 e28dd004 e59d4000 e28dd004 e12fff1e
  //   contents of rom_7 (hex, n*v repeats v):
  //   e3a00007 e3a0d080 e08dd00d e08dd00d eb000000 eafffffe e24dd004 e58d4000 e24dd004 e58d5000 e24dd004
  //   e58de000 e3500001 ca000000 ea000007 e1a04000 e2400001 ebfffff3 e1a05000 e1a00004 e2400002 ebffffef
  //   e0850000 e59de000 e28dd004 e59d5000 e28dd004 e59d4000 e28dd004 e12fff1e
  //   contents of rom_8 (hex, n*v repeats v):
  //   e5910000 e5814000 e2800004 e2444005 e1a04000 eaffffff ebffffff e12fff1e
endmodule

module DataMemory (
  input  clk,
  input  WE,
  input  RESET,
  input  [31:0] Address,
  input  [31:0] WORD,
  output [31:0] Read_Data
);

  wire not_1_out;

  // Probe on Address
  // Probe on WORD
  not not_1 (not_1_out, WE);
  RAM #(.dataWidth(32), .bus("separate")) ram_1 (
    .addr(Address[9:2]), .din(WORD), .data(Read_Data), .str(WE), .sel(1'b1), .clk(clk), .ld(not_1_out),
    .clr(RESET));
  // Probe on Read_Data
  // Probe on Read_Data
endmodule

// ALU Condition
module ALU_Condition_Flags (
  input  [1:0] ALU_Coltrol,
  input  [31:0] _32_A,
  input  [31:0] _32_B,
  output [31:0] _32_OUT,
  output ZERO___Z,
  output CARRY___C,
  output NEGATIVE___N,
  output OVERFLOW___V
);

  wire adder_1_cout, not_1_out, xnor_1_out, xor_1_out;
  wire [31:0] adder_1_out, and_1_out, not_2_out, or_1_out, subtractor_1_out;

  // Probe on _32_A
  // Probe on _32_B
  not not_1 (not_1_out, ALU_Coltrol[1]);
  xor xor_1 (xor_1_out, adder_1_out[31], _32_A[31]);
  Adder #(.width(32)) adder_1 (.a(_32_A), .b(_32_B), .out(adder_1_out), .cout(adder_1_cout));  // open: cin
  Subtractor #(.width(32)) subtractor_1 (.a(_32_A), .b(_32_B), .out(subtractor_1_out));  // open: bin, bout
  assign and_1_out = _32_A & _32_B;  // AND_Gate and_1, 32 bits wide
  assign or_1_out = _32_A | _32_B;  // OR_Gate or_1, 32 bits wide
  NotExactlyOne xnor_1 (.out(xnor_1_out), .in0(_32_B[31]), .in1(_32_A[31]), .in2(ALU_Coltrol[0]));
  and and_2 (CARRY___C, adder_1_cout, not_1_out);
  and and_3 (OVERFLOW___V, not_1_out, xor_1_out, xnor_1_out);
  Multiplexer #(.select(2), .width(32), .disabled(0), .enable("false")) multiplexer_1 (
    .in0(adder_1_out), .in1(subtractor_1_out), .in2(and_1_out), .in3(or_1_out), .out(_32_OUT),
    .sel(ALU_Coltrol));
  // Probe on _32_OUT
  assign not_2_out = ~_32_OUT;  // NOT_Gate not_2, 32 bits wide
  and and_4 (ZERO___Z, not_2_out[0], not_2_out[1], not_2_out[2], not_2_out[3], not_2_out[4], not_2_out[5], not_2_out[6], not_2_out[7], not_2_out[8], not_2_out[9], not_2_out[10], not_2_out[11], not_2_out[12], not_2_out[13], not_2_out[14], not_2_out[15], not_2_out[16], not_2_out[17], not_2_out[18], not_2_out[19], not_2_out[20], not_2_out[21], not_2_out[22], not_2_out[23], not_2_out[24], not_2_out[25], not_2_out[26], not_2_out[27], not_2_out[28], not_2_out[29], not_2_out[30], not_2_out[31]);

  assign NEGATIVE___N = _32_OUT[31];
endmodule

module SR_Latch (
  input  in_1,
  input  R,
  input  S,
  output Q,
  output Q_NOT
);

  wire nor_1_out, nor_2_out, not_1_out;

  nor nor_1 (nor_1_out, R, Q_NOT);
  nor nor_2 (nor_2_out, Q, S);
  not not_1 (not_1_out, in_1);
  and and_1 (Q, nor_1_out, not_1_out);
  or or_1 (Q_NOT, nor_2_out, in_1);
endmodule

module D_Latch (
  input  RESET,
  input  D,
  input  C,
  output Q,
  output NOT_Q
);

  wire and_1_out, and_2_out, not_1_out;

  not not_1 (not_1_out, D);
  and and_1 (and_1_out, not_1_out, C);
  and and_2 (and_2_out, D, C);
  SR_Latch sr_latch_1 (.R(and_1_out), .S(and_2_out), .Q(Q), .Q_NOT(NOT_Q), .in_1(RESET));
endmodule

module D_Flip_Flop (
  input  RESET,
  input  D,
  input  C,
  output Q,
  output NOT_Q
);

  wire d_latch_1_q, not_1_out;

  not not_1 (not_1_out, C);
  D_Latch d_latch_1 (.D(D), .C(not_1_out), .Q(d_latch_1_q), .RESET(RESET));  // open: NOT_Q
  D_Latch d_latch_2 (.D(d_latch_1_q), .C(C), .Q(Q), .NOT_Q(NOT_Q), .RESET(RESET));
endmodule

// EXTENDER
module Extender (
  input  [1:0] ImmSrc,
  input  [23:0] _24_IN,
  output [31:0] _32_OUT
);

  Multiplexer #(.select(2), .width(32)) multiplexer_1 (
    .in0({{24{1'b0}}, _24_IN[7:0]}), .in1({{20{1'b0}}, _24_IN[11:0]}),
    .in2({{7{_24_IN[23]}}, _24_IN[22:0], 2'b00}), .out(_32_OUT), .sel(ImmSrc));  // open: in3, en
endmodule

module Memory_Decoder (
  input  [31:0] _32_IN,
  output [11:0] Src2_12_Bit,
  output [11:0] imm12_12_Bit,
  output [3:0] Rm_4_Bit,
  output _0_1_Bit,
  output [1:0] sh_2_Bit,
  output [4:0] shamt5_5_Bit,
  output [3:0] Rd_4_Bit,
  output [3:0] Rn_4_Bit,
  output L,
  output W,
  output B,
  output U,
  output P,
  output nI,
  output [1:0] op_2_Bit,
  output [3:0] cond_4_Bit
);


  assign _0_1_Bit = _32_IN[4];
  assign B = _32_IN[22];
  assign cond_4_Bit = _32_IN[31:28];
  assign imm12_12_Bit = _32_IN[11:0];
  assign L = _32_IN[20];
  assign nI = _32_IN[25];
  assign op_2_Bit = _32_IN[27:26];
  assign P = _32_IN[24];
  assign Rd_4_Bit = _32_IN[15:12];
  assign Rm_4_Bit = _32_IN[3:0];
  assign Rn_4_Bit = _32_IN[19:16];
  assign sh_2_Bit = _32_IN[6:5];
  assign shamt5_5_Bit = _32_IN[11:7];
  assign Src2_12_Bit = _32_IN[11:0];
  assign U = _32_IN[23];
  assign W = _32_IN[21];

  // Notes on the sheet:
  //   IMMEDIATE
  //   REGISTER
  //   CORE
endmodule

// REGISTER FILE
module Register_File (
  input  [31:0] WD3,
  input  WE,
  input  [3:0] A3,
  input  [31:0] R15,
  input  [3:0] A1,
  input  [3:0] A2,
  input  CLOCK,
  input  RESET,
  output [31:0] r0,
  output [31:0] r1,
  output [31:0] r2,
  output [31:0] r3,
  output [31:0] r4,
  output [31:0] r5,
  output [31:0] r6,
  output [31:0] r7,
  output [31:0] r8,
  output [31:0] r9,
  output [31:0] r10,
  output [31:0] r11,
  output [31:0] r12,
  output [31:0] r13,
  output [31:0] r14,
  output [31:0] r15_2,
  output [31:0] R1_2,
  output [31:0] R2_2
);

  wire decoder_1_out0, decoder_1_out1, decoder_1_out2, decoder_1_out3, decoder_1_out4, decoder_1_out5,
       decoder_1_out6, decoder_1_out7, decoder_1_out8, decoder_1_out9, decoder_1_out10, decoder_1_out11,
       decoder_1_out12, decoder_1_out13, decoder_1_out14;

  Decoder_part #(.select(4), .disabled(0)) decoder_1 (
    .out0(decoder_1_out0), .out1(decoder_1_out1), .out2(decoder_1_out2), .out3(decoder_1_out3),
    .out4(decoder_1_out4), .out5(decoder_1_out5), .out6(decoder_1_out6), .out7(decoder_1_out7),
    .out8(decoder_1_out8), .out9(decoder_1_out9), .out10(decoder_1_out10), .out11(decoder_1_out11),
    .out12(decoder_1_out12), .out13(decoder_1_out13), .out14(decoder_1_out14), .sel(A3), .en(WE));  // open: out15
  Register #(.width(32)) register_1 (.D(WD3), .en(decoder_1_out0), .Q(r0), .clk(CLOCK), .clr(RESET));
  Register #(.width(32)) register_2 (.D(WD3), .en(decoder_1_out1), .Q(r1), .clk(CLOCK), .clr(RESET));
  Register #(.width(32)) register_3 (.D(WD3), .en(decoder_1_out2), .Q(r2), .clk(CLOCK), .clr(RESET));
  Register #(.width(32)) register_4 (.D(WD3), .en(decoder_1_out3), .Q(r3), .clk(CLOCK), .clr(RESET));
  Register #(.width(32)) register_5 (.D(WD3), .en(decoder_1_out4), .Q(r4), .clk(CLOCK), .clr(RESET));
  Register #(.width(32)) register_6 (.D(WD3), .en(decoder_1_out5), .Q(r5), .clk(CLOCK), .clr(RESET));
  Register #(.width(32)) register_7 (.D(WD3), .en(decoder_1_out6), .Q(r6), .clk(CLOCK), .clr(RESET));
  Register #(.width(32)) register_8 (.D(WD3), .en(decoder_1_out7), .Q(r7), .clk(CLOCK), .clr(RESET));
  Register #(.width(32)) register_9 (.D(WD3), .en(decoder_1_out8), .Q(r8), .clk(CLOCK), .clr(RESET));
  Register #(.width(32)) register_10 (.D(WD3), .en(decoder_1_out9), .Q(r9), .clk(CLOCK), .clr(RESET));
  Register #(.width(32)) register_11 (.D(WD3), .en(decoder_1_out10), .Q(r10), .clk(CLOCK), .clr(RESET));
  Register #(.width(32)) register_12 (.D(WD3), .en(decoder_1_out11), .Q(r11), .clk(CLOCK), .clr(RESET));
  Register #(.width(32)) register_13 (.D(WD3), .en(decoder_1_out12), .Q(r12), .clk(CLOCK), .clr(RESET));
  Register #(.width(32)) register_14 (.D(WD3), .en(decoder_1_out13), .Q(r13), .clk(CLOCK), .clr(RESET));
  Register #(.width(32)) register_15 (.D(WD3), .en(decoder_1_out14), .Q(r14), .clk(CLOCK), .clr(RESET));
  Multiplexer #(.select(4), .width(32), .disabled(0)) multiplexer_1 (
    .in0(r0), .in1(r1), .in2(r2), .in3(r3), .in4(r4), .in5(r5), .in6(r6), .in7(r7), .in8(r8), .in9(r9),
    .in10(r10), .in11(r11), .in12(r12), .in13(r13), .in14(r14), .in15(R15), .out(R1_2), .sel(A1), .en(1'b1));
  Multiplexer #(.select(4), .width(32), .disabled(0)) multiplexer_2 (
    .in0(r0), .in1(r1), .in2(r2), .in3(r3), .in4(r4), .in5(r5), .in6(r6), .in7(r7), .in8(r8), .in9(r9),
    .in10(r10), .in11(r11), .in12(r12), .in13(r13), .in14(r14), .in15(R15), .out(R2_2), .sel(A2), .en(1'b1));

  assign r15_2 = R15;
endmodule

// Main Decoder
module Main_Decoder (
  input  [1:0] OP,
  input  [5:0] Funct,
  input  [23:0] IW24,
  input  [31:0] IW,
  output Branch__BR,
  output REGW__RW,
  output MemtoReg__M2R,
  output MemW__MW,
  output ALUSrc__AS,
  output [1:0] immSrc__IS,
  output IsLDR,
  output IsSTR,
  output isBXLR,
  output [1:0] RegSrc__RS,
  output ALUOp__AO
);

  wire comparator_1_eq, DP_imm_out, DP_Reg_out;

  Comparator #(.width(24)) comparator_1 (.a(IW24), .b(24'h12fff1), .eq(comparator_1_eq));  // open: gt, lt
  Comparator #(.width(32)) comparator_2 (.a(IW), .b(32'he12fff1e), .eq(isBXLR));  // open: gt, lt
  and DP_Reg (DP_Reg_out, ~OP[0], ~OP[1], ~Funct[5], ~comparator_1_eq);  // AND_Gate
  and DP_imm (DP_imm_out, ~OP[0], ~OP[1], Funct[5], ~comparator_1_eq);  // AND_Gate
  and STR (IsSTR, OP[0], ~OP[1], ~Funct[0], ~comparator_1_eq);  // AND_Gate
  and LDR (IsLDR, OP[0], ~OP[1], Funct[0], ~comparator_1_eq);  // AND_Gate
  and B (Branch__BR, ~OP[0], OP[1]);  // AND_Gate
  or or_1 (REGW__RW, DP_Reg_out, DP_imm_out, IsLDR);
  or or_2 (ALUSrc__AS, DP_imm_out, IsSTR, IsLDR, Branch__BR);
  or or_3 (immSrc__IS[0], IsSTR, IsLDR);
  or or_4 (ALUOp__AO, DP_Reg_out, DP_imm_out);

  assign immSrc__IS[1] = Branch__BR;
  assign MemtoReg__M2R = IsLDR;
  assign MemW__MW = IsSTR;
  assign RegSrc__RS = {IsSTR, Branch__BR};
endmodule

// ALU Decoder
module ALU_Decoder (
  input  ALUOp,
  input  [4:0] Funct,
  output [1:0] FlagW,
  output IsCMP,
  output [1:0] ALUControl,
  output IsMov,
  output IsLink
);

  wire ADD_out, and_2_out, and_3_out, and_6_out, and_7_out, AND_out, CMP_out, MOV_out, ORR_out, SUB_out;

  and ADD (ADD_out, ~Funct[1], ~Funct[2], Funct[3], ~Funct[4]);  // AND_Gate
  and SUB (SUB_out, ~Funct[1], Funct[2], ~Funct[3], ~Funct[4]);  // AND_Gate
  and CMP (CMP_out, ~Funct[1], Funct[2], ~Funct[3], Funct[4]);  // AND_Gate
  and MOV (MOV_out, Funct[1], ~Funct[2], Funct[3], Funct[4]);  // AND_Gate
  and AND (AND_out, ~Funct[1], ~Funct[2], ~Funct[3], ~Funct[4]);  // AND_Gate
  and ORR (ORR_out, ~Funct[1], ~Funct[2], Funct[3], Funct[4]);  // AND_Gate
  and and_2 (and_2_out, ADD_out, ALUOp);
  and and_3 (and_3_out, SUB_out, ALUOp);
  and and_4 (IsCMP, CMP_out, ALUOp);
  and and_5 (IsMov, MOV_out, ALUOp);
  and and_6 (and_6_out, AND_out, ALUOp);
  and and_7 (and_7_out, ORR_out, ALUOp);
  or or_1 (FlagW[0], and_2_out, and_3_out, IsCMP, IsMov);
  or or_2 (ALUControl[0], and_3_out, IsCMP, and_7_out);
  or or_3 (ALUControl[1], and_6_out, and_7_out);

  assign FlagW[1] = Funct[0];
  assign IsLink = Funct[4];
endmodule

module PC_Logic (
  input  [3:0] Rd,
  input  RegW,
  input  Branch,
  output PCS
);

  wire and_1_out, comparator_1_eq;

  Comparator #(.width(4)) comparator_1 (.a(Rd), .b(4'b1111), .eq(comparator_1_eq));  // open: gt, lt
  and and_1 (and_1_out, comparator_1_eq, RegW);
  or or_1 (PCS, and_1_out, Branch);
endmodule

module Decoder (
  input  [3:0] Rd,
  input  [1:0] Op,
  input  [23:0] imm24,
  input  [5:0] Funct,
  input  [31:0] _32_in,
  output PCS,
  output IsB,
  output IsBLink,
  output RegW,
  output MemtoReg,
  output MemW,
  output ALUSrc,
  output [1:0] ImmSrc,
  output [1:0] RegSrc,
  output isBXLR,
  output IsLDR,
  output IsSTR,
  output [1:0] FlagW,
  output [1:0] ALUControl,
  output IsMov,
  output IsCMP
);

  wire alu_decoder_1_islink, main_decoder_1_aluop__ao, main_decoder_1_branch__br;

  PC_Logic pc_logic_1 (.Rd(Rd), .PCS(PCS), .RegW(RegW), .Branch(main_decoder_1_branch__br));
  Main_Decoder main_decoder_1 (
    .OP(Op), .Funct(Funct), .IW24(imm24), .Branch__BR(main_decoder_1_branch__br), .MemtoReg__M2R(MemtoReg),
    .MemW__MW(MemW), .ALUSrc__AS(ALUSrc), .immSrc__IS(ImmSrc), .RegSrc__RS(RegSrc),
    .ALUOp__AO(main_decoder_1_aluop__ao), .REGW__RW(RegW), .isBXLR(isBXLR), .IW(_32_in), .IsLDR(IsLDR),
    .IsSTR(IsSTR));
  ALU_Decoder alu_decoder_1 (
    .ALUOp(main_decoder_1_aluop__ao), .Funct(Funct[4:0]), .FlagW(FlagW), .ALUControl(ALUControl),
    .IsMov(IsMov), .IsLink(alu_decoder_1_islink), .IsCMP(IsCMP));
  and and_1 (IsBLink, main_decoder_1_branch__br, alu_decoder_1_islink);
  and and_2 (IsB, ~alu_decoder_1_islink, main_decoder_1_branch__br);  // AND_Gate

  // Other names for the same wires on the sheet: IW[31:0] = _32_in
endmodule

// GATE
module PC_Gate (
  input  [31:0] PC,
  input  CLock,
  input  Reset,
  output [31:0] PC_OUT
);

  Register #(.width(32)) register_1 (.D(PC), .en(CLock), .Q(PC_OUT), .clk(CLock), .clr(Reset));
endmodule

// Conditional Logic
module conditional_logic (
  input  PCS,
  input  RegW,
  input  MemW,
  input  CLOCK,
  input  [3:0] Cond,
  input  [3:0] ALUFlags,
  input  [1:0] FlagW,
  output PCSrc,
  output RegWrite,
  output MemWrite
);

  wire and_1_out, and_2_out, condition_check_1_condex;
  wire [1:0] register_1_q, register_2_q;

  Register #(.width(2)) register_1 (.D(ALUFlags[3:2]), .en(and_2_out), .Q(register_1_q), .clk(CLOCK));  // open: clr
  Register #(.width(2)) register_2 (.D(ALUFlags[1:0]), .en(and_1_out), .Q(register_2_q), .clk(CLOCK));  // open: clr
  and and_1 (and_1_out, FlagW[0], condition_check_1_condex);
  and and_2 (and_2_out, FlagW[1], condition_check_1_condex);
  and and_3 (PCSrc, PCS, condition_check_1_condex);
  and and_4 (RegWrite, RegW, condition_check_1_condex);
  and and_5 (MemWrite, MemW, condition_check_1_condex);
  Condition_Check condition_check_1 (
    .Cond(Cond), ._3_2(register_1_q), ._1_0(register_2_q), .CondEx(condition_check_1_condex));
endmodule

// Control
module Controller (
  input  CLOCK,
  input  [3:0] Cond,
  input  [3:0] ALUFlags,
  input  [3:0] RD,
  input  [1:0] OP,
  input  [23:0] imm24,
  input  [5:0] Funct,
  input  [31:0] IW,
  output PCSrc,
  output IsSTR,
  output IsLDR,
  output RegWrite,
  output MemWrite,
  output MemtoReg,
  output ALUSrc,
  output [1:0] ImmSrc,
  output [1:0] RegSrc,
  output [1:0] ALUControl,
  output IsMov,
  output IsBLink,
  output IsCMP,
  output IsBXLR,
  output IsB
);

  wire conditional_logic_1_regwrite, decoder_1_memw, decoder_1_pcs, decoder_1_regw, multiplexer_1_out;
  wire [1:0] decoder_1_flagw;

  Decoder decoder_1 (
    .Rd(RD), .Op(OP), .imm24(imm24), .Funct(Funct), .PCS(decoder_1_pcs), .RegW(decoder_1_regw),
    .MemtoReg(MemtoReg), .MemW(decoder_1_memw), .ALUSrc(ALUSrc), .ImmSrc(ImmSrc), .RegSrc(RegSrc),
    .FlagW(decoder_1_flagw), .ALUControl(ALUControl), .IsMov(IsMov), .IsBLink(IsBLink), .IsCMP(IsCMP),
    .isBXLR(IsBXLR), ._32_in(IW), .IsLDR(IsLDR), .IsSTR(IsSTR), .IsB(IsB));
  conditional_logic conditional_logic_1 (
    .PCS(decoder_1_pcs), .RegW(decoder_1_regw), .MemW(decoder_1_memw), .CLOCK(CLOCK), .Cond(Cond),
    .ALUFlags(ALUFlags), .FlagW(decoder_1_flagw), .PCSrc(PCSrc), .RegWrite(conditional_logic_1_regwrite),
    .MemWrite(MemWrite));
  Multiplexer #(.disabled(0), .enable("false")) multiplexer_1 (
    .in0(conditional_logic_1_regwrite), .in1(1'b1), .out(multiplexer_1_out), .sel(IsBLink));
  Multiplexer #(.disabled(0), .enable("false")) multiplexer_2 (
    .in0(multiplexer_1_out), .in1(1'b0), .out(RegWrite), .sel(IsCMP));
endmodule

module _15_12 (
  input  [31:0] IW,
  output [3:0] _15_12
);


  assign _15_12 = IW[15:12];
endmodule

module _25_20 (
  input  [31:0] IW,
  output [5:0] _25_20
);


  assign _25_20 = IW[25:20];
endmodule

module _27_26 (
  input  [31:0] IW,
  output [1:0] _27_26
);


  assign _27_26 = IW[27:26];
endmodule

module _31_28 (
  input  [31:0] IW,
  output [3:0] _31_28
);


  assign _31_28 = IW[31:28];
endmodule

module _23_0 (
  input  [31:0] IW,
  output [23:0] out_2
);


  assign out_2 = IW[23:0];
endmodule

module _19_16 (
  input  [31:0] in_1,
  output [3:0] out_2
);


  assign out_2 = in_1[19:16];
endmodule

module _3_0 (
  input  [31:0] IW,
  output [3:0] _15_12
);


  assign _15_12 = IW[3:0];
endmodule

module Condition_Check (
  input  [3:0] Cond,
  input  [1:0] _3_2,
  input  [1:0] _1_0,
  output CondEx
);

  wire and_1_out, and_2_out, and_3_out, and_4_out, and_5_out, comparator_1_eq, comparator_2_eq,
       comparator_3_eq, comparator_4_eq, comparator_5_eq, xnor_1_out;

  Comparator #(.width(4)) comparator_1 (.a(4'b0000), .b(Cond), .eq(comparator_1_eq));  // open: gt, lt
  Comparator #(.width(4)) comparator_2 (.a(4'b0001), .b(Cond), .eq(comparator_2_eq));  // open: gt, lt
  Comparator #(.width(4)) comparator_3 (.a(4'b1010), .b(Cond), .eq(comparator_3_eq));  // open: gt, lt
  Comparator #(.width(4)) comparator_4 (.a(4'b1100), .b(Cond), .eq(comparator_4_eq));  // open: gt, lt
  Comparator #(.width(4)) comparator_5 (.a(Cond), .b(4'b1110), .eq(comparator_5_eq));  // open: gt, lt
  // Probe on _3_2[1]
  // Probe on _3_2[0]
  // Probe on _1_0[0]
  // Probe on _1_0[1]
  xnor xnor_1 (xnor_1_out, _3_2[1], _1_0[0]);
  and and_1 (and_1_out, xnor_1_out, ~_3_2[0]);  // AND_Gate
  and and_2 (and_2_out, comparator_1_eq, _3_2[0]);
  and and_3 (and_3_out, comparator_2_eq, ~_3_2[0]);  // AND_Gate
  and and_4 (and_4_out, comparator_3_eq, xnor_1_out);
  and and_5 (and_5_out, comparator_4_eq, and_1_out);
  or or_1 (CondEx, and_2_out, and_3_out, comparator_5_eq, and_4_out, and_5_out);
endmodule

module RegisterLogic (
  input  IsBLink,
  input  IsBXLR,
  input  _0Bit,
  input  _1Bit,
  input  [31:0] IW,
  input  [31:0] PC_4,
  input  [31:0] OUTPUT,
  input  [31:0] PC_8,
  input  [31:0] r14,
  output [3:0] A2,
  output [3:0] A1,
  output [3:0] A3,
  output [31:0] WD3,
  output [31:0] r15
);

  wire [3:0] A2_t, A3_t, n3_0_1__15_12, n19_16_1_out_2;

  _19_16 u_19_16_1 (.in_1(IW), .out_2(n19_16_1_out_2));
  _3_0 u_3_0_1 (.IW(IW), ._15_12(n3_0_1__15_12));
  _15_12 u_15_12_1 (.IW(IW), ._15_12(A3_t));
  Multiplexer #(.width(4), .disabled(0), .enable("false")) multiplexer_1 (
    .in0(n19_16_1_out_2), .in1(4'b1111), .out(A1), .sel(_0Bit));
  Multiplexer #(.width(32), .disabled(0), .enable("false")) multiplexer_2 (
    .in0(PC_8), .in1(r14), .out(r15), .sel(IsBXLR));
  Multiplexer #(.width(4), .disabled(0), .enable("false")) multiplexer_3 (
    .in0(n3_0_1__15_12), .in1(A3_t), .out(A2_t), .sel(_1Bit));
  Multiplexer #(.width(32), .enable("false")) multiplexer_4 (.in0(OUTPUT), .in1(PC_4), .out(WD3), .sel(IsBLink));
  // Probe on A3_t
  Multiplexer #(.width(4), .disabled(0), .enable("false")) multiplexer_5 (
    .in0(A3_t), .in1(4'b1110), .out(A3), .sel(IsBLink));
  Multiplexer #(.width(4), .disabled(0), .enable("false")) multiplexer_6 (
    .in0(A2_t), .in1(4'b1111), .out(A2), .sel(IsBXLR));

  // Other names for the same wires on the sheet: BLink = IsBLink
endmodule

module PC_Adder (
  input  [31:0] PC,
  output [31:0] PC_4,
  output [31:0] PC_8
);

  wire adder_1_cout;

  Adder #(.width(32)) adder_1 (.a(PC), .b(32'h4), .out(PC_4), .cin(1'b0), .cout(adder_1_cout));
  Adder #(.width(32)) adder_2 (.a(PC_4), .b(32'h4), .out(PC_8), .cin(1'b0));  // open: cout
endmodule

module ALU_PreLogic (
  input  ALUSrc,
  input  IsMov,
  input  IsBXLR,
  input  [31:0] R1,
  input  [31:0] R2,
  input  [31:0] EXTEND,
  output [31:0] _32_1,
  output [31:0] _32_2
);

  wire or_1_out;

  or or_1 (or_1_out, IsMov, IsBXLR);
  Multiplexer #(.width(32), .disabled(0), .enable("false")) multiplexer_1 (
    .in0(R1), .in1({32{1'b0}}), .out(_32_1), .sel(or_1_out));
  Multiplexer #(.width(32), .disabled(0), .enable("false")) multiplexer_2 (
    .in0(R2), .in1(EXTEND), .out(_32_2), .sel(ALUSrc));
endmodule

// DONE
module Is_Done (
  input  PCSrc,
  input  [31:0] OLD_PC,
  input  [31:0] NEW_PC,
  output DONE
);

  wire comparator_1_eq;

  Comparator #(.width(32)) comparator_1 (.a(OLD_PC), .b(NEW_PC), .eq(comparator_1_eq));  // open: gt, lt
  and and_1 (DONE, PCSrc, comparator_1_eq);
endmodule

module ANSWER (
  input  [31:0] r0,
  input  [1:0] _2_In,
  output [31:0] ANSWER,
  output POWER_OUT
);

  Multiplexer #(.width(32), .disabled(0), .enable("false")) multiplexer_1 (
    .in0({32{1'b0}}), .in1(r0), .out(ANSWER), .sel(_2_In[0]));
  Multiplexer #(.disabled(0), .enable("false")) multiplexer_2 (
    .in0(1'b0), .in1(_2_In[1]), .out(POWER_OUT), .sel(_2_In[0]));

  // Other names for the same wires on the sheet: DONE = _2_In[0]
endmodule

module Visualizer (
  input  Is_LDR,
  input  Is_STR,
  input  Is_ADD,
  input  Is_SUB,
  input  Is_Mov,
  input  Is_B,
  input  Is_BL,
  input  Is_BX,
  input  Is_CMP,
  output [19:0] out_10,
  output [19:0] out_11,
  output [19:0] out_12,
  output [19:0] out_13,
  output [19:0] out_14,
  output [19:0] out_15,
  output [19:0] out_16,
  output [19:0] out_17,
  output [19:0] out_18
);

  wire [19:0] A1, A2, A3, B1, B2, B3, C1, C2, C3, D1, D2, D3, L1, L2, L3, M1, M2, M3, multiplexer_1_out,
       multiplexer_2_out, multiplexer_3_out, multiplexer_4_out, multiplexer_5_out, multiplexer_6_out,
       multiplexer_7_out, multiplexer_8_out, multiplexer_9_out, multiplexer_10_out, multiplexer_11_out,
       multiplexer_12_out, multiplexer_13_out, multiplexer_14_out, multiplexer_15_out, multiplexer_16_out,
       multiplexer_17_out, multiplexer_18_out, multiplexer_19_out, multiplexer_20_out, multiplexer_21_out,
       multiplexer_22_out, multiplexer_23_out, multiplexer_24_out, multiplexer_25_out, multiplexer_26_out,
       multiplexer_27_out, multiplexer_28_out, multiplexer_29_out, multiplexer_30_out, multiplexer_31_out,
       multiplexer_32_out, multiplexer_33_out, multiplexer_34_out, multiplexer_35_out, multiplexer_36_out,
       multiplexer_37_out, multiplexer_38_out, multiplexer_39_out, multiplexer_40_out, multiplexer_41_out,
       multiplexer_42_out, multiplexer_43_out, multiplexer_44_out, multiplexer_45_out, multiplexer_46_out,
       multiplexer_47_out, multiplexer_48_out, multiplexer_49_out, multiplexer_50_out, multiplexer_51_out,
       multiplexer_52_out, multiplexer_53_out, multiplexer_54_out, multiplexer_55_out, multiplexer_56_out,
       multiplexer_57_out, multiplexer_58_out, multiplexer_59_out, multiplexer_60_out, multiplexer_61_out,
       multiplexer_62_out, multiplexer_63_out, multiplexer_64_out, multiplexer_65_out, multiplexer_66_out,
       multiplexer_67_out, multiplexer_68_out, multiplexer_69_out, multiplexer_70_out, multiplexer_71_out,
       multiplexer_72_out, O1, O2, O3, P1, P2, P3, R1, R2, R3, S1, S2, S3, T1, T2, T3, U1, U2, U3, V1, V2,
       V3, X1, X2, X3;

  Multiplexer #(.width(20), .disabled(0), .enable("false")) multiplexer_1 (
    .in0({20{1'b0}}), .in1(L1), .out(multiplexer_1_out), .sel(Is_LDR));
  Multiplexer #(.width(20), .disabled(0), .enable("false")) multiplexer_2 (
    .in0({20{1'b0}}), .in1(L2), .out(multiplexer_2_out), .sel(Is_LDR));
  Multiplexer #(.width(20), .disabled(0), .enable("false")) multiplexer_3 (
    .in0({20{1'b0}}), .in1(L3), .out(multiplexer_3_out), .sel(Is_LDR));
  Multiplexer #(.width(20), .disabled(0), .enable("false")) multiplexer_4 (
    .in0({20{1'b0}}), .in1(D1), .out(multiplexer_4_out), .sel(Is_LDR));
  Multiplexer #(.width(20), .disabled(0), .enable("false")) multiplexer_5 (
    .in0({20{1'b0}}), .in1(D2), .out(multiplexer_5_out), .sel(Is_LDR));
  Multiplexer #(.width(20), .disabled(0), .enable("false")) multiplexer_6 (
    .in0({20{1'b0}}), .in1(D3), .out(multiplexer_6_out), .sel(Is_LDR));
  Multiplexer #(.width(20), .disabled(0), .enable("false")) multiplexer_7 (
    .in0({20{1'b0}}), .in1(R1), .out(multiplexer_7_out), .sel(Is_LDR));
  Multiplexer #(.width(20), .disabled(0), .enable("false")) multiplexer_8 (
    .in0({20{1'b0}}), .in1(R2), .out(multiplexer_8_out), .sel(Is_LDR));
  Multiplexer #(.width(20), .disabled(0), .enable("false")) multiplexer_9 (
    .in0({20{1'b0}}), .in1(R3), .out(multiplexer_9_out), .sel(Is_LDR));
  Multiplexer #(.width(20), .disabled(0), .enable("false")) multiplexer_10 (
    .in0(multiplexer_1_out), .in1(S1), .out(multiplexer_10_out), .sel(Is_STR));
  Multiplexer #(.width(20), .disabled(0), .enable("false")) multiplexer_11 (
    .in0(multiplexer_2_out), .in1(S2), .out(multiplexer_11_out), .sel(Is_STR));
  Multiplexer #(.width(20), .disabled(0), .enable("false")) multiplexer_12 (
    .in0(multiplexer_3_out), .in1(S3), .out(multiplexer_12_out), .sel(Is_STR));
  Multiplexer #(.width(20), .disabled(0), .enable("false")) multiplexer_13 (
    .in0(multiplexer_4_out), .in1(T1), .out(multiplexer_13_out), .sel(Is_STR));
  Multiplexer #(.width(20), .disabled(0), .enable("false")) multiplexer_14 (
    .in0(multiplexer_5_out), .in1(T2), .out(multiplexer_14_out), .sel(Is_STR));
  Multiplexer #(.width(20), .disabled(0), .enable("false")) multiplexer_15 (
    .in0(multiplexer_6_out), .in1(T3), .out(multiplexer_15_out), .sel(Is_STR));
  Multiplexer #(.width(20), .disabled(0), .enable("false")) multiplexer_16 (
    .in0(multiplexer_7_out), .in1(R1), .out(multiplexer_16_out), .sel(Is_STR));
  Multiplexer #(.width(20), .disabled(0), .enable("false")) multiplexer_17 (
    .in0(multiplexer_8_out), .in1(R2), .out(multiplexer_17_out), .sel(Is_STR));
  Multiplexer #(.width(20), .disabled(0), .enable("false")) multiplexer_18 (
    .in0(multiplexer_9_out), .in1(R3), .out(multiplexer_18_out), .sel(Is_STR));
  Multiplexer #(.width(20), .disabled(0), .enable("false")) multiplexer_19 (
    .in0(multiplexer_10_out), .in1(A1), .out(multiplexer_19_out), .sel(Is_ADD));
  Multiplexer #(.width(20), .disabled(0), .enable("false")) multiplexer_20 (
    .in0(multiplexer_11_out), .in1(A2), .out(multiplexer_20_out), .sel(Is_ADD));
  Multiplexer #(.width(20), .disabled(0), .enable("false")) multiplexer_21 (
    .in0(multiplexer_12_out), .in1(A3), .out(multiplexer_21_out), .sel(Is_ADD));
  Multiplexer #(.width(20), .disabled(0), .enable("false")) multiplexer_22 (
    .in0(multiplexer_13_out), .in1(D1), .out(multiplexer_22_out), .sel(Is_ADD));
  Multiplexer #(.width(20), .disabled(0), .enable("false")) multiplexer_23 (
    .in0(multiplexer_14_out), .in1(D2), .out(multiplexer_23_out), .sel(Is_ADD));
  Multiplexer #(.width(20), .disabled(0), .enable("false")) multiplexer_24 (
    .in0(multiplexer_15_out), .in1(D3), .out(multiplexer_24_out), .sel(Is_ADD));
  Multiplexer #(.width(20), .disabled(0), .enable("false")) multiplexer_25 (
    .in0(multiplexer_16_out), .in1(D1), .out(multiplexer_25_out), .sel(Is_ADD));
  Multiplexer #(.width(20), .disabled(0), .enable("false")) multiplexer_26 (
    .in0(multiplexer_17_out), .in1(D2), .out(multiplexer_26_out), .sel(Is_ADD));
  Multiplexer #(.width(20), .disabled(0), .enable("false")) multiplexer_27 (
    .in0(multiplexer_18_out), .in1(D3), .out(multiplexer_27_out), .sel(Is_ADD));
  Letters letters_1 (
    .M2(M2), .M3(M3), .M1(M1), .S1(S1), .S2(S2), .S3(S3), .B1(B1), .B2(B2), .B3(B3), .A1(A1), .A2(A2),
    .A3(A3), .T1(T1), .T2(T2), .T3(T3), .U1(U1), .U2(U2), .U3(U3), .R1(R1), .R2(R2), .R3(R3), .D1(D1),
    .D2(D2), .D3(D3), .L1(L1), .L2(L2), .L3(L3), .V1(V1), .V2(V2), .V3(V3), .O1(O1), .O2(O2), .O3(O3),
    .X1(X1), .X2(X2), .X3(X3), .P1(P1), .p2(P2), .P3(P3), .C1(C1), .C2(C2), .C3(C3));
  Multiplexer #(.width(20), .disabled(0), .enable("false")) multiplexer_28 (
    .in0(multiplexer_19_out), .in1(S1), .out(multiplexer_28_out), .sel(Is_SUB));
  Multiplexer #(.width(20), .disabled(0), .enable("false")) multiplexer_29 (
    .in0(multiplexer_20_out), .in1(S2), .out(multiplexer_29_out), .sel(Is_SUB));
  Multiplexer #(.width(20), .disabled(0), .enable("false")) multiplexer_30 (
    .in0(multiplexer_21_out), .in1(S3), .out(multiplexer_30_out), .sel(Is_SUB));
  Multiplexer #(.width(20), .disabled(0), .enable("false")) multiplexer_31 (
    .in0(multiplexer_22_out), .in1(U1), .out(multiplexer_31_out), .sel(Is_SUB));
  Multiplexer #(.width(20), .disabled(0), .enable("false")) multiplexer_32 (
    .in0(multiplexer_23_out), .in1(U2), .out(multiplexer_32_out), .sel(Is_SUB));
  Multiplexer #(.width(20), .disabled(0), .enable("false")) multiplexer_33 (
    .in0(multiplexer_24_out), .in1(U3), .out(multiplexer_33_out), .sel(Is_SUB));
  Multiplexer #(.width(20), .disabled(0), .enable("false")) multiplexer_34 (
    .in0(multiplexer_25_out), .in1(B1), .out(multiplexer_34_out), .sel(Is_SUB));
  Multiplexer #(.width(20), .disabled(0), .enable("false")) multiplexer_35 (
    .in0(multiplexer_26_out), .in1(B2), .out(multiplexer_35_out), .sel(Is_SUB));
  Multiplexer #(.width(20), .disabled(0), .enable("false")) multiplexer_36 (
    .in0(multiplexer_27_out), .in1(B3), .out(multiplexer_36_out), .sel(Is_SUB));
  Multiplexer #(.width(20), .disabled(0), .enable("false")) multiplexer_37 (
    .in0(multiplexer_28_out), .in1(M1), .out(multiplexer_37_out), .sel(Is_Mov));
  Multiplexer #(.width(20), .disabled(0), .enable("false")) multiplexer_38 (
    .in0(multiplexer_29_out), .in1(M2), .out(multiplexer_38_out), .sel(Is_Mov));
  Multiplexer #(.width(20), .disabled(0), .enable("false")) multiplexer_39 (
    .in0(multiplexer_30_out), .in1(M3), .out(multiplexer_39_out), .sel(Is_Mov));
  Multiplexer #(.width(20), .disabled(0), .enable("false")) multiplexer_40 (
    .in0(multiplexer_31_out), .in1(O1), .out(multiplexer_40_out), .sel(Is_Mov));
  Multiplexer #(.width(20), .disabled(0), .enable("false")) multiplexer_41 (
    .in0(multiplexer_32_out), .in1(O2), .out(multiplexer_41_out), .sel(Is_Mov));
  Multiplexer #(.width(20), .disabled(0), .enable("false")) multiplexer_42 (
    .in0(multiplexer_33_out), .in1(O3), .out(multiplexer_42_out), .sel(Is_Mov));
  Multiplexer #(.width(20), .disabled(0), .enable("false")) multiplexer_43 (
    .in0(multiplexer_34_out), .in1(V1), .out(multiplexer_43_out), .sel(Is_Mov));
  Multiplexer #(.width(20), .disabled(0), .enable("false")) multiplexer_44 (
    .in0(multiplexer_35_out), .in1(V2), .out(multiplexer_44_out), .sel(Is_Mov));
  Multiplexer #(.width(20), .disabled(0), .enable("false")) multiplexer_45 (
    .in0(multiplexer_36_out), .in1(V3), .out(multiplexer_45_out), .sel(Is_Mov));
  Multiplexer #(.width(20), .disabled(0), .enable("false")) multiplexer_46 (
    .in0(multiplexer_37_out), .in1({20{1'b0}}), .out(multiplexer_46_out), .sel(Is_B));
  Multiplexer #(.width(20), .disabled(0), .enable("false")) multiplexer_47 (
    .in0(multiplexer_38_out), .in1({20{1'b0}}), .out(multiplexer_47_out), .sel(Is_B));
  Multiplexer #(.width(20), .disabled(0), .enable("false")) multiplexer_48 (
    .in0(multiplexer_39_out), .in1({20{1'b0}}), .out(multiplexer_48_out), .sel(Is_B));
  Multiplexer #(.width(20), .disabled(0), .enable("false")) multiplexer_49 (
    .in0(multiplexer_40_out), .in1({20{1'b0}}), .out(multiplexer_49_out), .sel(Is_B));
  Multiplexer #(.width(20), .disabled(0), .enable("false")) multiplexer_50 (
    .in0(multiplexer_41_out), .in1({20{1'b0}}), .out(multiplexer_50_out), .sel(Is_B));
  Multiplexer #(.width(20), .disabled(0), .enable("false")) multiplexer_51 (
    .in0(multiplexer_42_out), .in1({20{1'b0}}), .out(multiplexer_51_out), .sel(Is_B));
  Multiplexer #(.width(20), .disabled(0), .enable("false")) multiplexer_52 (
    .in0(multiplexer_43_out), .in1(B1), .out(multiplexer_52_out), .sel(Is_B));
  Multiplexer #(.width(20), .disabled(0), .enable("false")) multiplexer_53 (
    .in0(multiplexer_44_out), .in1(B2), .out(multiplexer_53_out), .sel(Is_B));
  Multiplexer #(.width(20), .disabled(0), .enable("false")) multiplexer_54 (
    .in0(multiplexer_45_out), .in1(B3), .out(multiplexer_54_out), .sel(Is_B));
  Multiplexer #(.width(20), .disabled(0), .enable("false")) multiplexer_55 (
    .in0(multiplexer_46_out), .in1({20{1'b0}}), .out(multiplexer_55_out), .sel(Is_BL));
  Multiplexer #(.width(20), .disabled(0), .enable("false")) multiplexer_56 (
    .in0(multiplexer_47_out), .in1({20{1'b0}}), .out(multiplexer_56_out), .sel(Is_BL));
  Multiplexer #(.width(20), .disabled(0), .enable("false")) multiplexer_57 (
    .in0(multiplexer_48_out), .in1({20{1'b0}}), .out(multiplexer_57_out), .sel(Is_BL));
  Multiplexer #(.width(20), .disabled(0), .enable("false")) multiplexer_58 (
    .in0(multiplexer_49_out), .in1(B1), .out(multiplexer_58_out), .sel(Is_BL));
  Multiplexer #(.width(20), .disabled(0), .enable("false")) multiplexer_59 (
    .in0(multiplexer_50_out), .in1(B2), .out(multiplexer_59_out), .sel(Is_BL));
  Multiplexer #(.width(20), .disabled(0), .enable("false")) multiplexer_60 (
    .in0(multiplexer_51_out), .in1(B3), .out(multiplexer_60_out), .sel(Is_BL));
  Multiplexer #(.width(20), .disabled(0), .enable("false")) multiplexer_61 (
    .in0(multiplexer_52_out), .in1(L1), .out(multiplexer_61_out), .sel(Is_BL));
  Multiplexer #(.width(20), .disabled(0), .enable("false")) multiplexer_62 (
    .in0(multiplexer_53_out), .in1(L2), .out(multiplexer_62_out), .sel(Is_BL));
  Multiplexer #(.width(20), .disabled(0), .enable("false")) multiplexer_63 (
    .in0(multiplexer_54_out), .in1(L3), .out(multiplexer_63_out), .sel(Is_BL));
  Multiplexer #(.width(20), .disabled(0), .enable("false")) multiplexer_64 (
    .in0(multiplexer_55_out), .in1({20{1'b0}}), .out(multiplexer_64_out), .sel(Is_BX));
  Multiplexer #(.width(20), .disabled(0), .enable("false")) multiplexer_65 (
    .in0(multiplexer_56_out), .in1({20{1'b0}}), .out(multiplexer_65_out), .sel(Is_BX));
  Multiplexer #(.width(20), .disabled(0), .enable("false")) multiplexer_66 (
    .in0(multiplexer_57_out), .in1({20{1'b0}}), .out(multiplexer_66_out), .sel(Is_BX));
  Multiplexer #(.width(20), .disabled(0), .enable("false")) multiplexer_67 (
    .in0(multiplexer_58_out), .in1(B1), .out(multiplexer_67_out), .sel(Is_BX));
  Multiplexer #(.width(20), .disabled(0), .enable("false")) multiplexer_68 (
    .in0(multiplexer_59_out), .in1(B2), .out(multiplexer_68_out), .sel(Is_BX));
  Multiplexer #(.width(20), .disabled(0), .enable("false")) multiplexer_69 (
    .in0(multiplexer_60_out), .in1(B3), .out(multiplexer_69_out), .sel(Is_BX));
  Multiplexer #(.width(20), .disabled(0), .enable("false")) multiplexer_70 (
    .in0(multiplexer_61_out), .in1(X1), .out(multiplexer_70_out), .sel(Is_BX));
  Multiplexer #(.width(20), .disabled(0), .enable("false")) multiplexer_71 (
    .in0(multiplexer_62_out), .in1(X2), .out(multiplexer_71_out), .sel(Is_BX));
  Multiplexer #(.width(20), .disabled(0), .enable("false")) multiplexer_72 (
    .in0(multiplexer_63_out), .in1(X3), .out(multiplexer_72_out), .sel(Is_BX));
  Multiplexer #(.width(20), .disabled(0), .enable("false")) multiplexer_73 (
    .in0(multiplexer_64_out), .in1(C1), .out(out_10), .sel(Is_CMP));
  Multiplexer #(.width(20), .disabled(0), .enable("false")) multiplexer_74 (
    .in0(multiplexer_65_out), .in1(C2), .out(out_11), .sel(Is_CMP));
  Multiplexer #(.width(20), .disabled(0), .enable("false")) multiplexer_75 (
    .in0(multiplexer_66_out), .in1(C3), .out(out_12), .sel(Is_CMP));
  Multiplexer #(.width(20), .disabled(0), .enable("false")) multiplexer_76 (
    .in0(multiplexer_67_out), .in1(M1), .out(out_13), .sel(Is_CMP));
  Multiplexer #(.width(20), .disabled(0), .enable("false")) multiplexer_77 (
    .in0(multiplexer_68_out), .in1(M2), .out(out_14), .sel(Is_CMP));
  Multiplexer #(.width(20), .disabled(0), .enable("false")) multiplexer_78 (
    .in0(multiplexer_69_out), .in1(M3), .out(out_15), .sel(Is_CMP));
  Multiplexer #(.width(20), .disabled(0), .enable("false")) multiplexer_79 (
    .in0(multiplexer_70_out), .in1(P1), .out(out_16), .sel(Is_CMP));
  Multiplexer #(.width(20), .disabled(0), .enable("false")) multiplexer_80 (
    .in0(multiplexer_71_out), .in1(P2), .out(out_17), .sel(Is_CMP));
  Multiplexer #(.width(20), .disabled(0), .enable("false")) multiplexer_81 (
    .in0(multiplexer_72_out), .in1(P3), .out(out_18), .sel(Is_CMP));
endmodule

module Letters (
  output [19:0] M1,
  output [19:0] M2,
  output [19:0] M3,
  output [19:0] B1,
  output [19:0] B2,
  output [19:0] B3,
  output [19:0] T1,
  output [19:0] T2,
  output [19:0] T3,
  output [19:0] S1,
  output [19:0] S2,
  output [19:0] S3,
  output [19:0] A1,
  output [19:0] A2,
  output [19:0] A3,
  output [19:0] U1,
  output [19:0] U2,
  output [19:0] U3,
  output [19:0] P1,
  output [19:0] p2,
  output [19:0] P3,
  output [19:0] R1,
  output [19:0] R2,
  output [19:0] R3,
  output [19:0] D1,
  output [19:0] D2,
  output [19:0] D3,
  output [19:0] L1,
  output [19:0] L2,
  output [19:0] L3,
  output [19:0] C1,
  output [19:0] C2,
  output [19:0] C3,
  output [19:0] V1,
  output [19:0] V2,
  output [19:0] V3,
  output [19:0] O1,
  output [19:0] O2,
  output [19:0] O3,
  output [19:0] X1,
  output [19:0] X2,
  output [19:0] X3
);

  DotMatrix #(.matrixcols(6), .matrixrows(10)) dotmatrix_1 (
    .col0(10'h1ff), .col1(10'h80), .col2(10'h40), .col3(10'h80), .col4(10'h1ff), .col5({10{1'b0}}));
  DotMatrix #(.matrixcols(6), .matrixrows(10)) dotmatrix_2 (
    .col0({10{1'b0}}), .col1(10'h1f1), .col2(10'h111), .col3(10'h111), .col4(10'h11f), .col5({10{1'b0}}));
  DotMatrix #(.matrixcols(6), .matrixrows(10)) dotmatrix_3 (
    .col0({10{1'b0}}), .col1(10'h1ff), .col2(10'h11c), .col3(10'h116), .col4(10'hf3), .col5({10{1'b0}}));
  DotMatrix #(.matrixcols(6), .matrixrows(10)) dotmatrix_4 (
    .col0({10{1'b0}}), .col1(10'h1fc), .col2(10'h3), .col3(10'h3), .col4(10'h1fc), .col5({10{1'b0}}));
  DotMatrix #(.matrixcols(6), .matrixrows(10)) dotmatrix_5 (
    .col0({10{1'b0}}), .col1(10'h1ff), .col2(10'h111), .col3(10'h111), .col4(10'hee), .col5({10{1'b0}}));
  DotMatrix #(.matrixcols(6), .matrixrows(10)) dotmatrix_6 (
    .col0({10{1'b0}}), .col1(10'hff), .col2(10'h190), .col3(10'h190), .col4(10'hff), .col5({10{1'b0}}));
  DotMatrix #(.matrixcols(6), .matrixrows(10)) dotmatrix_7 (
    .col0({10{1'b0}}), .col1(10'h1ff), .col2(10'h101), .col3(10'h101), .col4(10'hfe), .col5({10{1'b0}}));
  DotMatrix #(.matrixcols(6), .matrixrows(10)) dotmatrix_8 (
    .col0({10{1'b0}}), .col1(10'hfe), .col2(10'h101), .col3(10'h101), .col4(10'hfe), .col5({10{1'b0}}));
  DotMatrix #(.matrixcols(6), .matrixrows(10)) dotmatrix_9 (
    .col0({10{1'b0}}), .col1(10'h100), .col2(10'h1ff), .col3(10'h1ff), .col4(10'h100), .col5({10{1'b0}}));
  DotMatrix #(.matrixcols(6), .matrixrows(10)) dotmatrix_10 (
    .col0({10{1'b0}}), .col1(10'h1ff), .col2(10'h1), .col3(10'h1), .col4(10'h1ff), .col5({10{1'b0}}));
  DotMatrix #(.matrixcols(6), .matrixrows(10)) dotmatrix_11 (
    .col0({10{1'b0}}), .col1(10'h1ff), .col2(10'h1), .col3(10'h1), .col4(10'h1), .col5({10{1'b0}}));
  DotMatrix #(.matrixcols(6), .matrixrows(10)) dotmatrix_12 (
    .col0(10'h101), .col1(10'hc6), .col2(10'h38), .col3(10'h38), .col4(10'hc6), .col5(10'h101));
  DotMatrix #(.matrixcols(6), .matrixrows(10)) dotmatrix_13 (
    .col0({10{1'b0}}), .col1(10'h1ff), .col2(10'h110), .col3(10'h110), .col4(10'he0), .col5({10{1'b0}}));
  DotMatrix #(.matrixcols(6), .matrixrows(10)) dotmatrix_14 (
    .col0({10{1'b0}}), .col1(10'h1ff), .col2(10'h101), .col3(10'h101), .col4(10'h101), .col5({10{1'b0}}));

  assign A1 = 20'hff;
  assign A2 = 20'h64190;
  assign A3 = 20'h3fc00;
  assign B1 = 20'h1ff;
  assign B2 = 20'h44511;
  assign B3 = 20'h3b800;
  assign C1 = 20'h1ff;
  assign C2 = 20'h40501;
  assign C3 = 20'h40400;
  assign D1 = 20'h1ff;
  assign D2 = 20'h40501;
  assign D3 = 20'h3f800;
  assign L1 = 20'h1ff;
  assign L2 = 20'h401;
  assign L3 = 20'h400;
  assign M1 = 20'h7fc80;
  assign M2 = 20'h10080;
  assign M3 = 20'h7fc00;
  assign O1 = 20'hfe;
  assign O2 = 20'h40501;
  assign O3 = 20'h3f800;
  assign P1 = 20'h1ff;
  assign p2 = 20'h44110;
  assign P3 = 20'h38000;
  assign R1 = 20'h1ff;
  assign R2 = 20'h47116;
  assign R3 = 20'h3cc00;
  assign S1 = 20'h1f1;
  assign S2 = 20'h44511;
  assign S3 = 20'h47c00;
  assign T1 = 20'h100;
  assign T2 = 20'h7fdff;
  assign T3 = 20'h40000;
  assign U1 = 20'h1ff;
  assign U2 = 20'h401;
  assign U3 = 20'h7fc00;
  assign V1 = 20'h1fc;
  assign V2 = 20'hc03;
  assign V3 = 20'h7f000;
  assign X1 = 20'h404c6;
  assign X2 = 20'he038;
  assign X3 = 20'h31901;
endmodule

module CheckADDSUB (
  input  [31:0] IW,
  output IsAdd,
  output IsSub
);

  Comparator #(.width(4)) comparator_1 (.a(IW[24:21]), .b(4'b0100), .eq(IsAdd));  // open: gt, lt
  Comparator #(.width(4)) comparator_2 (.a(IW[24:21]), .b(4'b0010), .eq(IsSub));  // open: gt, lt
endmodule
